# Fritzing sketch SketchArduinoHourGlass (saved by Fritzing 0.9.6b)

parts:
  Bauteil1 = Arduino Mega 2560 (Rev3)
  MPU6050 = InvenSense MPU6050
  M2 = MAX7219 8x8 single Led Matrix Module
  8x8_LED-Matrix_mit_MAX7219_Treiberplatine = MAX7219 8x8 single Led Matrix Module

nets:
  N1: Bauteil1.D21/SCL, MPU6050.SCL
  N2: Bauteil1.D20/SDA, MPU6050.SDA
  N3: Bauteil1.D13_PWM, M2.I-VCC, 8x8_LED-Matrix_mit_MAX7219_Treiberplatine.I-VCC, 8x8_LED-Matrix_mit_MAX7219_Treiberplatine.O-VCC
  N4: Bauteil1.D11_PWM, 8x8_LED-Matrix_mit_MAX7219_Treiberplatine.I-DIN
  N5: Bauteil1.D10_PWM, M2.I-GND, 8x8_LED-Matrix_mit_MAX7219_Treiberplatine.I-GND, 8x8_LED-Matrix_mit_MAX7219_Treiberplatine.O-GND
  3V3: Bauteil1.3V3, MPU6050.VCC
  N6: Bauteil1.5V, M2.I-CLK, 8x8_LED-Matrix_mit_MAX7219_Treiberplatine.I-CLK, 8x8_LED-Matrix_mit_MAX7219_Treiberplatine.O-CLK
  GND: Bauteil1.GND, MPU6050.GND, M2.I-CS, M2.O-CS, 8x8_LED-Matrix_mit_MAX7219_Treiberplatine.I-CS, 8x8_LED-Matrix_mit_MAX7219_Treiberplatine.O-CS
  N7: M2.I-DIN, 8x8_LED-Matrix_mit_MAX7219_Treiberplatine.O-DOUT

notes:
  VCC = Rot
  GND = Schwarz
  CL(K) = Gelb
  DA/DIN = Blau
  CS = Orange

custom parts:
  MAX7219 8x8 single Led Matrix Module: Description: MAX7219 8x8 LedMatrix single Red Module Dimensions: 32x32mm Documents:
